# Fritzing sketch SchematicOfMorseCode (saved by Fritzing 0.9.3b)
breadboards: 1

parts:
  Part1 = Arduino Uno (Rev3)
  S1 = Pushbutton [package=THT]
  S2 = Pushbutton [package=THT]
  LED1 = smd LED [color="Red (633nm)" package="1206 [SMD]"]
  J1 = Piezo Speaker
  R1 = Resistor [tolerance=±5% resistance=220 package=THT]
  R2 = Resistor [tolerance=±5% resistance=220 package=THT]
  R3 = Resistor [tolerance=±5% resistance=220 package=THT]
  R4 = Resistor [tolerance=±5% resistance=220 package=THT]

nets:
  N1: Part1.D8, R2.Pin_0
  N2: Part1.D12/MISO, R1.Pin_0
  N3: Part1.D2, S1.leg0, R4.Pin_1
  N4: Part1.D7, S2.leg0, R3.Pin_1
  N5: Part1.GND, LED1.cathode, J1.pin1, R3.Pin_0, R4.Pin_0
  N6: S1.leg1, S2.leg1
  N7: LED1.anode, R2.Pin_1
  N8: J1.pin2, R1.Pin_1
